# Fritzing sketch breadboard (saved by Fritzing 0.9.6b)
breadboards: 3

parts:
  U2 = 555 Timer [package="DIP8 [THT]"]
  R1 = Resistor [tolerance=±5% resistance=10k package="2512 [SMD]"]
  S1 = Pushbutton [package="[SMD]"]
  R2 = Resistor [tolerance=±5% resistance=10k package="2512 [SMD]"]
  S2 = Pushbutton [package="[SMD]"]
  U3 = 555 Timer [package="DIP8 [THT]"]
  LED1 = LED - 5mm [color="Red (633nm)" current=0.030 package="5 mm [THT]"]
  R3 = Resistor [tolerance=±5% resistance=470 package="2512 [SMD]"]  # not connected
  R5 = Resistor [tolerance=±5% resistance=100k power=0.25 package=THT]
  R6 = Resistor [tolerance=±5% resistance=100k power=0.25 package=THT]
  C1 = Capacitor [package=cap-pth-small2]
  C2 = Capacitor [package=cap-pth-small2]
  U4 = CD4026B [package=dil16]
  U6 = 7-SEGMENT-DISPLAY [package=7-segment-display]
  R7 = Resistor [tolerance=±5% resistance=10k package="2512 [SMD]"]
  S3 = Pushbutton [package="[SMD]"]
  U7 = CD4026B [package=dil16]
  U8 = CD4026B [package=dil16]
  U9 = 7-SEGMENT-DISPLAY [package=7-segment-display]
  R8 = Resistor [tolerance=±5% resistance=10k package="2512 [SMD]"]
  R11 = Resistor [tolerance=±5% resistance=10k package="2512 [SMD]"]
  U10 = 7-SEGMENT-DISPLAY [package=7-segment-display]
  R12 = Resistor [tolerance=±5% resistance=220 package="2512 [SMD]"]
  R13 = Resistor [tolerance=±5% resistance=220 package="2512 [SMD]"]
  R14 = Resistor [tolerance=±5% resistance=220 package="2512 [SMD]"]
  R15 = Resistor [tolerance=±5% resistance=220 package="2512 [SMD]"]
  C3 = Capacitor [package=cap-pth-small2]
  C4 = Capacitor [package=cap-pth-small2]

nets:
  GND: U2.Ground, U3.Ground, U3.Reset, U4.Y2, U4.Y3, U4.GND, U7.Y2, U7.Y3, U7.GND, U8.Y2, U8.Y3, U8.GND
  N1: U2.Trigger, R1.Pin_1, S1.Pin_3, S1.Pin_4
  N2: U2.Output, U3.Vcc_Supply_Voltage, R5.Pin_0
  N3: U2.Reset, R2.Pin_1, S2.Pin_3, S2.Pin_4, C4.1
  N4: U2.Threshold, LED1.anode, C1.2, C2.2, U4.X1, R7.Pin_0, U7.X1, U8.X1, R8.Pin_0, R11.Pin_0
  VCC: U2.Vcc_Supply_Voltage, U4.VCC, U7.VCC, U8.VCC
  N5: R1.Pin_0, R2.Pin_0, U4.Y, U7.Y, U8.Y
  N6: S1.Pin_1, S1.Pin_2, S2.Pin_1, S2.Pin_2, C4.2
  N7: U3.Trigger, U3.Threshold, R6.Pin_0, C1.1
  N8: U3.Output, U4.Y0
  N9: U3.Control_Voltage, C2.1
  N10: U3.Discharge, R5.Pin_1
  N11: U4.Y1, U7.Y0
  N12: U4.INH, U6.G
  N13: U4.VEE, U6.E
  N14: U4.B, U6.G1
  N15: U4.A, U6.G2
  N16: U4.X3, U6.D
  N17: U4.X0, U6.A
  N18: U4.X, U6.DP
  N19: U4.X2, R7.Pin_1, S3.Pin_3, S3.Pin_4, U7.X2, U8.X2, R8.Pin_1, R11.Pin_1, C3.1
  N20: U6.C, R14.Pin_0
  N21: S3.Pin_1, S3.Pin_2, C3.2
  N22: U7.Y1, U8.Y0
  N23: U7.INH, U9.G
  N24: U7.VEE, U9.E
  N25: U7.B, U9.G1
  N26: U7.A, U9.G2
  N27: U7.X3, U9.D
  N28: U7.X0, U9.A
  N29: U7.X, U9.DP
  N30: U8.INH, U10.G
  N31: U8.VEE, U10.E
  N32: U8.B, U10.G1
  N33: U8.A, U10.G2
  N34: U8.X3, U10.D
  N35: U8.X0, U10.A
  N36: U8.X, U10.DP
  N37: U9.C, R13.Pin_0
  N38: U9.B, R15.Pin_0
  N39: U10.C, R12.Pin_0
  N40: R12.Pin_1, R13.Pin_1, R14.Pin_1

custom parts:
  CD4026B: Dual 4:1 analog mux
